# Fritzing sketch modelo-de-montagem-fritzing (saved by Fritzing 0.9.3b)
circuit board: 8.46667cm x 5.64444cm
breadboards: 1

parts:
  RHT1 = Humidity and Temperature Sensor RHT03
  U1 = ESP8266 NodeMCU LoLin module
  R1 = Resistor [tolerance=±5% resistance=220 package=THT]
  OLED1 = OLED 128x64 I2C Monochrome Display GND-VDD

nets:
  VCC: RHT1.Vcc, U1.3V3, R1.Pin_0, OLED1.VDD
  N1: RHT1.Data-signal, U1.D3, R1.Pin_1
  GND: RHT1.GND_2, U1.GND, OLED1.GND
  N2: U1.D1, OLED1.SCK
  N3: U1.D2, OLED1.SDA

custom parts:
  ESP8266 NodeMCU LoLin module: ESP8266 based NodeMCU
  OLED 128x64 I2C Monochrome Display GND-VDD: OLED 128x64 I2C Monochrome Display. Note: there are two variants of this part, this one is the GND VDD SCK SDA variant. The other is VDD GND SCK SDA. Make sure you select the part that matches your module as using the incorrect part will probably destroy your module! In addition the mounting holes are marked on silkscreen but not by default drilled. If you want drilled mounting holes, copy a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

// code stored in the sketch: modelo-de-montagem.ino
#include <DHT.h>
#define DHTPIN D3
#define DHTTYPE DHT22


DHT dht(DHTPIN, DHTTYPE);


void setup() {
  Serial.begin(115200);
  


}


void loop() {
  int umidade = dht.readHumidity();
  int temperatura = dht.readTemperature(false);
  Serial.print("Temperatura: ");
  Serial.print(temperatura);
  Serial.print(" °C");
  Serial.print(" ");
  Serial.print("Umidade de ");
  Serial.println(umidade);
  delay(5000);


}
